// Digital circuit 2_Demux_1x4.dig as structural Verilog
module _2_Demux_1x4 (
  input  ENTRADA,
  input  Sel1,
  input  Sel0,
  output Output3,
  output Output2,
  output Output1,
  output Output0
);

  wire not_1_out, not_2_out;

  not not_1 (not_1_out, Sel1);
  not not_2 (not_2_out, Sel0);
  and and_1 (Output3, ENTRADA, Sel1, Sel0);
  and and_2 (Output2, ENTRADA, Sel1, not_2_out);
  and and_3 (Output1, ENTRADA, Sel0, not_1_out);
  and and_4 (Output0, ENTRADA, not_1_out, not_2_out);

  // Other names for the same wires on the sheet: Data = ENTRADA

  // Notes on the sheet:
  //   Mediante combinaciones binarias de los selectores se indica por cuál salida se va a ver reflejado el dato de entrada.
endmodule
