// Digital circuit 3_Flip_Flop_JK.dig as structural Verilog
module _3_Flip_Flop_JK (
  input  J,
  input  K,
  input  CLOCK,
  output Q,
  output Q_2
);

  wire nand_1_out, nand_2_out, nand_3_out, nand_4_out, nand_5_out, nand_6_out, nand_7_out, nand_8_out,
       not_1_out, not_2_out, not_3_out;

  nand nand_1 (nand_1_out, Q_2, J);
  nand nand_2 (nand_2_out, CLOCK, K);
  not not_1 (not_1_out, nand_1_out);
  not not_2 (not_2_out, nand_2_out);
  nand nand_3 (nand_3_out, not_1_out, CLOCK);
  nand nand_4 (nand_4_out, not_2_out, Q);
  not not_3 (not_3_out, CLOCK);
  nand nand_5 (nand_5_out, nand_3_out, nand_6_out);
  nand nand_6 (nand_6_out, nand_5_out, nand_4_out);
  nand nand_7 (nand_7_out, nand_5_out, not_3_out);
  nand nand_8 (nand_8_out, not_3_out, nand_6_out);
  nand nand_9 (Q, nand_7_out, Q_2);
  nand nand_10 (Q_2, Q, nand_8_out);

  // Other names for the same wires on the sheet: Q__feedback = Q_2; Q_feedback = Q

  // Notes on the sheet:
  //   J: default 1
  //   SOBRE EL FLIP FLOP JK
  //   Se construye usando dos SR Latch con enable. Se llama maestro al Latch por donde están las entradas y esclavo a donde están las salidas
  //   Su funcionamiento es muy similar al del SR: cuando la señal de reloj va de bajo a alto (flanco de subida) la información pasa al maestro y se queda almacenada ahí. 
  //   En el flanco de bajada, se habilita el esclavo y la información guardada en el maestro pasa hasta verse reflejada a la salida.
  //   En esta configuración se elimina el error del SR. Esto, porque las salidas retroalimentan las entradas.
  //   NOTA: en el maestro había que usar una NAND de 3 entradas, por lo que se utilizó las reglas para convertirla a compuertas de 2 entradas
  //   Cuando J está en alto, al cabo de un ciclo completo, Q se va a estar en alto también. 
  //   Mientras que K, actúa como el Reset, cuando está activo Q' estará en alto, por lo que Q va a estar en cero 
  //   En este caso, cuando J=K=1 la salida va a ir cambiando entre 1 y 0.
  //   Si ambas entradas están en cero, en la salida se va a conservar el último estado así el reloj siga avanzando.
  //   Esclavo
endmodule
