// Digital circuit 3_Flip_Flop_RS.dig as structural Verilog
module _3_Flip_Flop_RS (
  input  SET,
  input  RESET,
  input  CLOCK,
  output Q,
  output Q_2
);

  wire nand_1_out, nand_2_out, nand_3_out, nand_4_out, nand_5_out, nand_6_out, not_1_out;

  nand nand_1 (nand_1_out, SET, CLOCK);
  nand nand_2 (nand_2_out, CLOCK, RESET);
  not not_1 (not_1_out, CLOCK);
  nand nand_3 (nand_3_out, nand_1_out, nand_4_out);
  nand nand_4 (nand_4_out, nand_3_out, nand_2_out);
  nand nand_5 (nand_5_out, nand_3_out, not_1_out);
  nand nand_6 (nand_6_out, not_1_out, nand_4_out);
  nand nand_7 (Q, nand_5_out, Q_2);
  nand nand_8 (Q_2, Q, nand_6_out);

  // Notes on the sheet:
  //   SOBRE EL FLIP FLOP RS:
  //   Es la conexión en serie de dos "SR Latch con enable" Uno es llamado maestro (por donde están las entradas S,R) y el otro se llama esclavo (por donde están las salidas Q, Q').
  //   La clave de funciomamiento de este flip-flop es que sólo se dan cambios en la salida cuando se completa un ciclo de reloj (pasar de bajo-alto y de alto-bajo)
  //   Cuando la señal del reloj pasa de bajo a alto, se habilita el maestro y se "guarda" el estado de set o reset en esta parte del circuito. 
  //   Pero no se ve reflejada inmediatamente en Q, ya que, durante ese flanco, el esclavo está deshabilitado.
  //   Cuando la señal de reloj pasa de alto a bajo, se habilita el esclavo y la información que venía guardada puede seguir su camino hacia el esclavo y verse reflejada en Q. 
  //   Lo que hace posible que se alterne de esta manera entre el escalvo y el maestro es que la entrada de reloj del esclavo está negada con respecto a la del maestro. 
  //   CUIDADO: las entradas set y reset no pueden estar activadas al tiempo ya que el sistema queda indeterminado
  //   En esta configuración, el circuito de sincroniza cada ciclo completo de reloj. 
  //   Cuando el SET está en alto, Q también lo estará. 
  //   Cuando el RESET está en alto, Q' es el que estará en alto, por lo que Q quedará en cero.
  //   Si ambas entradas están en cero, el sistema va a conservar el último estado de la salida así el reloj siga avanzando.
  //   Maestro
  //   Esclavo
endmodule
