// Digital circuit 4_Pin_uso_general.dig as structural Verilog
module _4_Pin_uso_general (
  input  D_CONFIGURACION_3,
  input  D_CONFIGURACION_2,
  input  D_CONFIGURACION_1,
  input  D_CONFIGURACION_0,
  input  SET_C,
  input  Enable,
  input  CLEAR_C,
  input  ESTADO_S3,
  input  ESTADO_S2,
  input  ESTADO_S1,
  input  ESTADO_S0,
  input  SET_S,
  input  Enable_2,
  input  CLEAR_S,
  input  SET_A,
  input  Enable_3,
  input  CLEAR_A,
  input  RELOJ_DEL_SISTEMA,
  input  ENTRADA_PIN_0,
  input  ENTRADA_PIN_1,
  input  ENTRADA_PIN_2,
  input  ENTRADA_PIN_3,
  output GUARDAR_PIN3,
  output GUARDAR_PIN2,
  output GUARDAR_PIN1,
  output GUARDAR_PIN0
);

  wire ALMACENAR_PIN0, ALMACENAR_PIN1, ALMACENAR_PIN2, ALMACENAR_PIN3, d_ff_as_1_q, d_ff_as_5_q, d_ff_as_8_q,
       d_ff_as_11_q, driverinvsel_1_out, driverinvsel_2_out, driverinvsel_3_out, driverinvsel_4_out,
       ESTADO_PIN0, ESTADO_PIN1, ESTADO_PIN2, ESTADO_PIN3, multiplexer_1_out, multiplexer_2_out,
       multiplexer_3_out, multiplexer_4_out, multiplexer_5_out, multiplexer_6_out, multiplexer_7_out,
       multiplexer_8_out, multiplexer_9_out, multiplexer_10_out, multiplexer_11_out, multiplexer_12_out;

  PullDown pulldown_1 (.out(ALMACENAR_PIN3));
  Multiplexer multiplexer_1 (.sel(Enable), .in_0(d_ff_as_1_q), .in_1(D_CONFIGURACION_3), .out(multiplexer_1_out));
  Multiplexer multiplexer_2 (.sel(Enable_3), .in_0(GUARDAR_PIN3), .in_1(ALMACENAR_PIN3), .out(multiplexer_2_out));
  Multiplexer multiplexer_3 (.sel(Enable_2), .in_0(ESTADO_PIN3), .in_1(ESTADO_S3), .out(multiplexer_3_out));
  D_FF_AS d_ff_as_1 (
    .Set(SET_C), .D(multiplexer_1_out), .C(RELOJ_DEL_SISTEMA), .Clr(CLEAR_C), .Q(d_ff_as_1_q));  // open: nQ
  D_FF_AS d_ff_as_2 (
    .Set(SET_A), .D(multiplexer_2_out), .C(RELOJ_DEL_SISTEMA), .Clr(CLEAR_A), .Q(GUARDAR_PIN3));  // open: nQ
  D_FF_AS d_ff_as_3 (
    .Set(SET_S), .D(multiplexer_3_out), .C(RELOJ_DEL_SISTEMA), .Clr(CLEAR_S), .Q(ESTADO_PIN3));  // open: nQ
  assign driverinvsel_1_out = ~d_ff_as_1_q ? ESTADO_PIN3 : 1'bz;  // DriverInvSel driverinvsel_1
  PullDown pulldown_2 (.out(ALMACENAR_PIN2));
  LED SALIDA_PIN_3 (.in(driverinvsel_1_out));
  assign ALMACENAR_PIN3 = d_ff_as_1_q ? ENTRADA_PIN_3 : 1'bz;  // Driver driver_1
  Multiplexer multiplexer_4 (.sel(Enable_3), .in_0(GUARDAR_PIN2), .in_1(ALMACENAR_PIN2), .out(multiplexer_4_out));
  Multiplexer multiplexer_5 (.sel(Enable), .in_0(d_ff_as_5_q), .in_1(D_CONFIGURACION_2), .out(multiplexer_5_out));
  D_FF_AS d_ff_as_4 (
    .Set(SET_A), .D(multiplexer_4_out), .C(RELOJ_DEL_SISTEMA), .Clr(CLEAR_A), .Q(GUARDAR_PIN2));  // open: nQ
  Multiplexer multiplexer_6 (.sel(Enable_2), .in_0(ESTADO_PIN2), .in_1(ESTADO_S2), .out(multiplexer_6_out));
  D_FF_AS d_ff_as_5 (
    .Set(SET_C), .D(multiplexer_5_out), .C(RELOJ_DEL_SISTEMA), .Clr(CLEAR_C), .Q(d_ff_as_5_q));  // open: nQ
  PullDown pulldown_3 (.out(ALMACENAR_PIN1));
  assign driverinvsel_2_out = ~d_ff_as_5_q ? ESTADO_PIN2 : 1'bz;  // DriverInvSel driverinvsel_2
  D_FF_AS d_ff_as_6 (
    .Set(SET_S), .D(multiplexer_6_out), .C(RELOJ_DEL_SISTEMA), .Clr(CLEAR_S), .Q(ESTADO_PIN2));  // open: nQ
  LED SALIDA_PIN_2 (.in(driverinvsel_2_out));
  Multiplexer multiplexer_7 (.sel(Enable_3), .in_0(GUARDAR_PIN1), .in_1(ALMACENAR_PIN1), .out(multiplexer_7_out));
  assign ALMACENAR_PIN2 = d_ff_as_5_q ? ENTRADA_PIN_2 : 1'bz;  // Driver driver_2
  D_FF_AS d_ff_as_7 (
    .Set(SET_A), .D(multiplexer_7_out), .C(RELOJ_DEL_SISTEMA), .Clr(CLEAR_A), .Q(GUARDAR_PIN1));  // open: nQ
  Multiplexer multiplexer_8 (.sel(Enable), .in_0(d_ff_as_8_q), .in_1(D_CONFIGURACION_1), .out(multiplexer_8_out));
  PullDown pulldown_4 (.out(ALMACENAR_PIN0));
  D_FF_AS d_ff_as_8 (
    .Set(SET_C), .D(multiplexer_8_out), .C(RELOJ_DEL_SISTEMA), .Clr(CLEAR_C), .Q(d_ff_as_8_q));  // open: nQ
  Multiplexer multiplexer_9 (.sel(Enable_2), .in_0(ESTADO_PIN1), .in_1(ESTADO_S1), .out(multiplexer_9_out));
  assign driverinvsel_3_out = ~d_ff_as_8_q ? ESTADO_PIN1 : 1'bz;  // DriverInvSel driverinvsel_3
  Multiplexer multiplexer_10 (.sel(Enable_3), .in_0(GUARDAR_PIN0), .in_1(ALMACENAR_PIN0), .out(multiplexer_10_out));
  LED SALIDA_PIN_1 (.in(driverinvsel_3_out));
  D_FF_AS d_ff_as_9 (
    .Set(SET_A), .D(multiplexer_10_out), .C(RELOJ_DEL_SISTEMA), .Clr(CLEAR_A), .Q(GUARDAR_PIN0));  // open: nQ
  D_FF_AS d_ff_as_10 (
    .Set(SET_S), .D(multiplexer_9_out), .C(RELOJ_DEL_SISTEMA), .Clr(CLEAR_S), .Q(ESTADO_PIN1));  // open: nQ
  assign ALMACENAR_PIN1 = d_ff_as_8_q ? ENTRADA_PIN_1 : 1'bz;  // Driver driver_3
  Multiplexer multiplexer_11 (.sel(Enable), .in_0(d_ff_as_11_q), .in_1(D_CONFIGURACION_0), .out(multiplexer_11_out));
  D_FF_AS d_ff_as_11 (
    .Set(SET_C), .D(multiplexer_11_out), .C(RELOJ_DEL_SISTEMA), .Clr(CLEAR_C), .Q(d_ff_as_11_q));  // open: nQ
  assign driverinvsel_4_out = ~d_ff_as_11_q ? ESTADO_PIN0 : 1'bz;  // DriverInvSel driverinvsel_4
  Multiplexer multiplexer_12 (.sel(Enable_2), .in_0(ESTADO_PIN0), .in_1(ESTADO_S0), .out(multiplexer_12_out));
  LED SALIDA_PIN_0 (.in(driverinvsel_4_out));
  assign ALMACENAR_PIN0 = d_ff_as_11_q ? ENTRADA_PIN_0 : 1'bz;  // Driver driver_4
  D_FF_AS d_ff_as_12 (
    .Set(SET_S), .D(multiplexer_12_out), .C(RELOJ_DEL_SISTEMA), .Clr(CLEAR_S), .Q(ESTADO_PIN0));  // open: nQ

  // Other names for the same wires on the sheet: clock = RELOJ_DEL_SISTEMA

  // Notes on the sheet:
  //   Registro de configuración
  //   Registro de almacenamiento
  //   si el pin es de entrada
  //   Registro de control 
  //   si el pin es de salida
  //   En estas salidas "GUARDAR PINi" se ve reflejado 
  //   el dato que se guarda (lo que haya en "ENTRADA PIN i" 
  //   si el pin fue configurado como de entrada.
  //   Aquí se utilizó una resistencia de pull down para 
  //   poder garantizar un cero lógico cuando el registro
  //   de almacenamiento esté desconectado, ya que 
  //   tener un estado de alta impedancia no es lo mismo
  //   que tener un cero y cuando ese Z esta en la entrada
  //   del multiplexor actuaba como una indeterminación 
  //   y el registro actuaba de forma anormal.
  //   Con estos "ESTADOS Si" se indica lo que va
  //   a salir por el pin si está configurado
  //   como de salida
  //   SOBRE EL REGISTRO DE CONFIGURACIÓN
  //   - Si "D CONFIGURACIÓN i" está activo, significa que el pin va a ser de entrada. Como es de entrada, 
  //   lo que haya en el pin "ENTRADA PIN i" se va a propagar, a través del buffer tri state al registro de almacenamiento
  //   mediante el tuner "ALMACENAR PIN i".
  //   - Si "D CONFIGURACIÓN i" está inactivo, significa que el pin va a ser de salida. En este caso, a través del 
  //   buffer se va a propagar lo que venga del registro de control a través del tunel "ESTADO PIN i" hacia la 
  //   "SALIDA PIN i"
  //   CONSIDERACIONES GENERALES
  //   - En la vida real, la estructura física de un pin se puede configurar como de salida o de entrada según se desee. 
  //   En este caso, como el programa solo reconoce entradas O salidas, para un solo pin, se tiene por separado la 
  //   entrada y la salida. En la vida real, esos dos elementos separados realmente representa un mismo pin
  //   - Todos los registros están sincronizados con el mismo reloj
  //   Si el pin esta configurado como de
  //   salida, este estado (1/0) se va a
  //   propagar. En caso de ser 1, se va a 
  //   encender el LED a la salida y si es 0, no se va a
  //   prender
  //   EXPLICACIÓN DEL FUNCIONAMIENTO GENERAL:
  //   - Desde el registro de configuración, mediante la entrada "D CONFIGURACIÓN i"
  //   donde i es el número del pin, se configura si el pin 
  //   será de entrada o salida.
  //   Con el boton "SET_C" se puede poner indicar que 
  //   todos los pines sean de entrada al 
  //   tiempo, al contrario que con "CLEAR_C" todos se 
  //   configuran de salida.
  //   - Si es de entrada, el buffer tri state (no negado) conectado a Q
  //   va a quedar activo, por lo que, lo que haya en la entrada va a
  //   transmitirse mediante el tunel hacia la entrada del registro de
  //   almacenamiento, donde se verá reflejado en la salida 
  //   "GUARDAR PIN i" cuando el reloj actualice el sistema (en flancos 
  //   de subida)
  //   El botón "SET_A" hace que se guarde un 1 en cada bit del registro
  //   de almacenamiento
  //   mientras que "CLEAR_A" lleva a cero todas las salidas de ese registro
  //   - Si es de salida, el buffer tri state (negado) conectado, por lo que, 
  //   el estado que se haya configurado como de salida (mediante las entradas 
  //   "ESTADO SALIDA PIN i" en el registro de control) se va a ver reflejado en la 
  //   salida, que en este caso son unos LEDS de colores. 
  //   Con el botón "SET_S" se puede encender todos los LEDS al tiempo.
  //   Con el botón "CLEAR_S" se pueden apagar todos los LEDS al tiempo
endmodule
